# Fritzing sketch DiveIno (saved by Fritzing 0.9.3b)
breadboards: 2

parts:
  Part1 = Arduino Mega 2560 (Rev3)
  Part3 = Adafruit DS3231 [part_number="Adafruit #3013"]
  Part4 = PowerBoost 500 Charger
  S1 = Toggle Switch [package=THT]
  J1 = Piezo Speaker
  IR1 = TSOP312.., 314.. [package=THT]
  SparkFun_Pressure_Sensor_Breakout_-_MS5803-14BA1 = SparkFun Pressure Sensor Breakout - MS5803-14BA [part_number="SEN-12909 "]
  SparkFun_LiPo_Fuel_Gauge1 = SparkFun LiPo Fuel Gauge [part_number=TOL-10617]  # not connected
  J3 = female pin header, 3 pins [form="♀ (female)"]
  S2 = Reed switch [package=THT]
  Part2 = Adafruit Bluefruit LE UART Friend [part_number="Adafruit #2479"]
  Q1 = NPN-Transistor [package="TO92 [THT]"]
  R2 = Resistor [tolerance=±5% resistance=250k package=THT]
  R4 = Resistor [tolerance=±5% resistance=100k package=THT]
  J2 = female pin header, 4 pins [form="♀ (female)"]
  LED1 = LED - 5mm [color="Blue (430nm)" package="5 mm [THT]"]
  R5 = Resistor [tolerance=±5% resistance=220 package=THT]
  J4 = female pin header, 4 pins [form="♀ (female)"]
  R6 = Resistor [tolerance=±5% resistance=10k package=THT]
  J5 = female pin header, 2 pins [form="♀ (female)"]
  J6 = female pin header, 4 pins [form="♀ (female)"]
  R3 = Resistor [tolerance=±5% resistance=220 package=THT]

nets:
  N1: Part1.D11_PWM, IR1.Data, J4.pin3
  N2: Part1.D8_PWM, J1.pin2, J4.pin4
  VIN: Part1.3V3, Part3.Vin, IR1.Vs, SparkFun_Pressure_Sensor_Breakout_-_MS5803-14BA1.3.3V, J3.pin1, Part2.VIN, Part2.RXI, R4.Pin_0, J2.pin1, R3.Pin_0
  GND: Part1.GND, Part3.GND, Part4.GND, S1.L2, J1.pin1, IR1.GND, SparkFun_Pressure_Sensor_Breakout_-_MS5803-14BA1.GND, J3.pin2, S2.pin_1, Part2.GND, Part2.CTS, Q1.C, R2.Pin_0, LED1.cathode, J5.pin2, J6.pin3
  N3: Part1.VIN, Part4.5.0V, J3.pin3
  N4: Part1.D3_PWM, Q1.E, J4.pin2, R3.Pin_1
  N5: Part1.D6_PWM, R5.Pin_0, J4.pin1
  N6: Part3.SCL, SparkFun_Pressure_Sensor_Breakout_-_MS5803-14BA1.SCL/SCLK, J2.pin4
  N7: Part3.SDA, SparkFun_Pressure_Sensor_Breakout_-_MS5803-14BA1.SDA/SDI, J2.pin3
  N8: Part4.VBAT, R6.Pin_1
  N9: Part4.ENABLE, S1.COM, S2.pin_2, R6.Pin_0, J5.pin1, J6.pin4
  N10: Part2.TXO, J2.pin2
  N11: Q1.B, R2.Pin_1, J6.pin1
  N12: R4.Pin_1, J6.pin2
  N13: LED1.anode, R5.Pin_1

custom parts:
  Adafruit DS3231: The datasheet for the DS3231 explains that this part is an "Extremely Accurate I²C-Integrated RTC/TCXO/Crystal". And, hey, it does exactly what it says on the tin! This Real Time Clock (RTC) is the most precise you can get in a small, low power package. Most RTCs use an external 32kHz timing crystal that is used to keep time with low current draw. And that's all well and good, but those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
  PowerBoost 500 Charger: The PowerBoost 500C is a little DC/DC boost converter module that can be powered by any 3.7V LiIon/LiPoly battery, and convert the battery output to 5.2V DC for running your 5V projects. At its heart is a TPS61090 boost converter from TI. This boost converter chip has some really nice extras such as low battery detection, 2A internal switch, synchronous conversion, excellent efficiency, and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
  SparkFun Pressure Sensor Breakout - MS5803-14BA: This is the MS5803-14BA Pressure Sensor Breakout, a high resolution pressure sensor with both an I2C and SPI interface. This MEMS pressure sensor measures the absolute pressure of the fluid around it which includes air, water, and anything else that acts like a viscous fluid. Depending on how you interpret the data, you can determine altitude, water depth, or any other tasks that require an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
  SparkFun LiPo Fuel Gauge: LiPo batteries are a great way to power your projects. They’re small, lightweight, and pack a pretty good punch for their size. Unfortunately, even the best batteries eventually run low on power and when they do it’s often unexpected (and at the worst time). Don’t be caught by surprise next time your board suddenly powers-down! The SparkFun LiPo Fuel Gauge connects your battery to your project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
  Adafruit Bluefruit LE UART Friend: The Bluefruit LE UART Friend makes it easy to add Bluetooth Low Energy connectivity to anything with a hardware or software serial port. We even have nice hardware flow control so you won't have to think about losing data. Connect to your Arduino or other microcontroller or even just a standard FTDI cable for debugging and testing.
